// Logisim project GCD processor.circ as structural Verilog
module main (
  input  [4:0] in_1,
  input  [4:0] in_2,
  input  in_3,
  input  in_4,
  input  in_5,
  output [4:0] out_6,
  output [4:0] out_7
);

  wire clock_1_out, comparator_1_gt, comparator_1_lt, comparator_3_lt;
  wire [4:0] multiplexer_1_out, multiplexer_2_out, multiplexer_3_out, multiplexer_4_out, multiplexer_5_out,
       multiplexer_6_out, register_2_q;

  Clock clock_1 (.out(clock_1_out));
  Comparator_part #(.width(5), .mode("unsigned")) comparator_1 (
    .a(in_1), .b(in_2), .gt(comparator_1_gt), .lt(comparator_1_lt));  // open: eq
  Multiplexer #(.width(5), .enable("false")) multiplexer_1 (
    .in0(multiplexer_2_out), .in1(multiplexer_3_out), .out(multiplexer_1_out), .sel(in_3));
  Multiplexer #(.width(5), .enable("false")) multiplexer_2 (
    .in0(in_1), .in1(in_2), .out(multiplexer_2_out), .sel(comparator_1_lt));
  Register #(.width(5)) register_1 (.D(multiplexer_1_out), .en(in_5), .Q(out_6), .clk(clock_1_out));  // open: clr
  Multiplexer #(.width(5), .enable("false")) multiplexer_3 (
    .in0(out_7), .in1(register_2_q), .out(multiplexer_3_out), .sel(comparator_3_lt));
  Comparator comparator_2 (.in_1(out_6), .in_2(register_2_q), .out_3(out_7));
  Multiplexer #(.width(5), .enable("false")) multiplexer_4 (
    .in0(in_1), .in1(in_2), .out(multiplexer_4_out), .sel(comparator_1_gt));
  Multiplexer #(.width(5), .enable("false")) multiplexer_5 (
    .in0(multiplexer_4_out), .in1(multiplexer_6_out), .out(multiplexer_5_out), .sel(in_3));
  Register #(.width(5)) register_2 (
    .D(multiplexer_5_out), .en(in_4), .Q(register_2_q), .clk(clock_1_out));  // open: clr
  Multiplexer #(.width(5), .enable("false")) multiplexer_6 (
    .in0(register_2_q), .in1(out_7), .out(multiplexer_6_out), .sel(comparator_3_lt));
  Comparator_part #(.width(5), .mode("unsigned")) comparator_3 (
    .a(out_7), .b(register_2_q), .lt(comparator_3_lt));  // open: gt, eq

  // Notes on the sheet:
  //   INPUT X
  //   INPUT Y
  //   REG X
  //   GCD(X,Y)
  //   REG Y
  //   X-Y
  //   X>=Y
endmodule

module Comparator (
  input  [4:0] in_1,
  input  [4:0] in_2,
  output [4:0] out_3
);

  Subtractor #(.width(5)) subtractor_1 (.a(in_1), .b(in_2), .out(out_3));  // open: bin, bout
endmodule
